# Fritzing sketch D1_DHT2 (saved by Fritzing 0.9.3b)
breadboards: 1

parts:
  WeMos_D1_Mini1 = WeMos D1 Mini
  DHT1 = DHT11 Humitidy and Temperature Sensor

nets:
  5V: WeMos_D1_Mini1.5V, DHT1.VDD
  N1: WeMos_D1_Mini1.D1, DHT1.DATA
  N2: WeMos_D1_Mini1.G, DHT1.GND

custom parts:
  DHT11 Humitidy and Temperature Sensor: DHT11 Humidity and Temperature Sensor
